# Fritzing sketch electro (saved by Fritzing 0.9.2b)
breadboards: 1

parts:
  Part1 = Photon
  R2 = Resistor [tolerance=±1% resistance=10k package=THT]  # not connected
  R1 = Resistor [tolerance=±1% resistance=82k package=THT]

nets:
  N1: Part1.A5, R1.Pin_1
